# Fritzing sketch PCB[FritzingSketch] (saved by Fritzing 0.9.3b)
breadboards: 1

parts:
  Part1 = Arduino Uno (Rev3) - ICSP
  D1 = Rectifier Diode [part_number=1N4001 package="300 mil [THT]"]
  R1 = Resistor [tolerance=±5% resistance=220 package=THT]
  MIDI_In = MIDI_CONN_FEMALE [package=din_5_female]
  StartStop = AUDIO-JACK2 [package=audio-jack]
  Clock = AUDIO-JACK2 [package=audio-jack]
  Write = AUDIO-JACK2 [package=audio-jack]
  R2 = Resistor [tolerance=±5% resistance=10k package=THT]
  Trigger_Button = SWITCH-MOMENTARY-2 [package=tactile-pth-12mm]
  6N138 = IC, DIP package, 8 pins [chip_label=IC]

nets:
  N1: Part1.D0/RX, R2.Pin_1, 6N138.pin6
  N2: Part1.D2, Clock.TIP
  N3: Part1.D3_PWM, Write.TIP
  N4: Part1.D4, StartStop.TIP
  N5: Part1.D5_PWM, Trigger_Button.1
  N6: Part1.5V, R2.Pin_0, 6N138.pin8
  N7: Part1.GND, StartStop.SLEEVE, Clock.SLEEVE, Write.SLEEVE, Trigger_Button.2, 6N138.pin5
  N8: D1.cathode, R1.Pin_1, 6N138.pin2
  N9: D1.anode, MIDI_In.MIDI_IN, 6N138.pin3
  N10: R1.Pin_0, MIDI_In.MIDI_OUT
